# Fritzing sketch Untitled Sketch (saved by Fritzing 0.9.3b)
circuit board: 7.06074cm x 6.16029cm
breadboards: 1

parts:
  U1 = NodeMCU V1.0
  JP1 = Header 6 [package=molex-1x6-ra]
  JP2 = Header 3 [package=molex-1x3_lock]
  JP3 = Header 4 [package=molex-1x4_lock]
  JP4 = Header 4 [package=molex-1x4_lock]
  Q1 = PNP-Transistor [package="TO92 [THT]"]
  J1 = Camdenboss CTB0158-2 [part_number=CTB0158-2 package=THT]
  J2 = Camdenboss CTB0158-2 [part_number=CTB0158-2 package=THT]  # not connected

nets:
  N1: U1.D0, JP1.2
  N2: U1.D1, JP4.1
  N3: U1.D2, JP4.2
  N4: U1.D3, JP3.3
  N5: U1.D4, JP1.3
  N6: U1.GND, JP2.3, JP3.1, JP4.4, Q1.C, J1.pin2
  N7: U1.D5, JP3.4
  N8: U1.D6, JP2.2
  N9: U1.D7, J1.pin1
  N10: U1.D8, Q1.B
  N11: U1.Vin, JP1.5, JP2.1, JP3.2, JP4.3
  N12: JP1.4, Q1.E

custom parts:
  NodeMCU V1.0: ESP8266 based NodeMCU
